// Digital circuit 4-input_multiplexer.dig as structural Verilog
module _4_input_multiplexer (
  input  Input_4,
  input  Input_3,
  input  Input_2,
  input  Input_1,
  input  s_1,
  input  s_2,
  output Ouput
);

  wire and_1_out, and_2_out, and_3_out, and_4_out;

  and and_1 (and_1_out, ~s_1, ~s_2, Input_1);  // And
  and and_2 (and_2_out, ~s_1, s_2, Input_2);  // And
  and and_3 (and_3_out, ~s_2, s_1, Input_3);  // And
  and and_4 (and_4_out, s_2, s_1, Input_4);
  or or_1 (Ouput, and_1_out, and_2_out, and_3_out, and_4_out);
endmodule
