// Digital circuit 8_input_multiplexer.dig as structural Verilog
module _8_input_multiplexer (
  input  I_1,
  input  I_2,
  input  I_3,
  input  I_4,
  input  I_5,
  input  I_6,
  input  I_7,
  input  I_8,
  input  S_1,
  input  S_2,
  input  S_3,
  output out_12
);

  wire and_1_out, and_2_out, and_3_out, and_4_out, and_5_out, and_6_out, and_7_out, and_8_out, or_1_out,
       or_2_out;

  and and_1 (and_1_out, ~S_1, ~S_2, ~S_3, I_1);  // And
  and and_2 (and_2_out, ~S_1, ~S_2, S_3, I_2);  // And
  and and_3 (and_3_out, ~S_1, S_2, ~S_3, I_3);  // And
  and and_4 (and_4_out, ~S_1, S_2, S_3, I_4);  // And
  and and_5 (and_5_out, S_1, ~S_2, ~S_3, I_5);  // And
  and and_6 (and_6_out, S_1, ~S_2, S_3, I_6);  // And
  and and_7 (and_7_out, S_1, S_2, ~S_3, I_7);  // And
  and and_8 (and_8_out, S_1, S_2, S_3, I_8);
  or or_1 (or_1_out, and_1_out, and_2_out, and_3_out, and_4_out);
  or or_2 (or_2_out, and_5_out, and_6_out, and_7_out, and_8_out);
  or or_3 (out_12, or_1_out, or_2_out);
endmodule
