// Digital circuit ex4.dig as structural Verilog
module ex4 (
  input  Input_4,
  input  Input_3,
  input  Input_2,
  input  Input_1,
  input  s_1,
  input  s_2,
  input  a,
  input  b,
  output Ouput
);

  wire and_1_out, and_2_out, and_3_out, and_4_out, and_5_out, not_1_out, or_1_out, xor_1_out;

  and and_1 (and_1_out, a, b);
  or or_1 (or_1_out, a, b);
  xor xor_1 (xor_1_out, a, b);
  not not_1 (not_1_out, a);
  and and_2 (and_2_out, ~s_1, ~s_2, and_1_out);  // And
  and and_3 (and_3_out, ~s_1, s_2, or_1_out);  // And
  and and_4 (and_4_out, ~s_2, s_1, xor_1_out);  // And
  and and_5 (and_5_out, s_2, s_1, not_1_out);
  or or_2 (Ouput, and_2_out, and_3_out, and_4_out, and_5_out);
endmodule
