// Digital circuit parity_parity_generator.dig as structural Verilog
module parity_parity_generator (
  input  S_1,
  input  S_2,
  input  S_3,
  output out_4
);

  wire and_1_out, and_2_out, and_3_out, and_4_out, or_1_out, or_2_out;

  and and_1 (and_1_out, ~S_1, ~S_2, ~S_3);  // And
  and and_2 (and_2_out, ~S_1, S_2, S_3);  // And
  and and_3 (and_3_out, S_1, ~S_2, S_3);  // And
  and and_4 (and_4_out, S_1, S_2, ~S_3);  // And
  or or_1 (or_1_out, and_1_out, and_2_out);
  or or_2 (or_2_out, and_3_out, and_4_out);
  or or_3 (out_4, or_1_out, or_2_out);
endmodule
