// Digital circuit 4_bit_register_with_rorate.dig as structural Verilog
module _4_bit_register_with_rorate (
  input  clk,
  input  P_3,
  input  P_2,
  input  P_1,
  input  P_0,
  input  PRE,
  output D_3,
  output D_2,
  output D_1,
  output D_0
);

  wire and_1_out, and_2_out, and_3_out, and_4_out, and_5_out, and_6_out, and_7_out, and_8_out, not_1_out,
       or_1_out, or_2_out, or_3_out, or_4_out;

  not not_1 (not_1_out, PRE);
  and and_1 (and_1_out, D_0, not_1_out);
  and and_2 (and_2_out, PRE, P_3);
  and and_3 (and_3_out, D_3, not_1_out);
  and and_4 (and_4_out, P_2, PRE);
  and and_5 (and_5_out, D_2, not_1_out);
  and and_6 (and_6_out, P_1, PRE);
  and and_7 (and_7_out, D_1, not_1_out);
  and and_8 (and_8_out, P_0, PRE);
  or or_1 (or_1_out, and_1_out, and_2_out);
  or or_2 (or_2_out, and_3_out, and_4_out);
  or or_3 (or_3_out, and_5_out, and_6_out);
  or or_4 (or_4_out, and_7_out, and_8_out);
  D_FF d_ff_1 (.D(or_1_out), .C(clk), .Q(D_3));  // open: nQ
  D_FF d_ff_2 (.D(or_2_out), .C(clk), .Q(D_2));  // open: nQ
  D_FF d_ff_3 (.D(or_3_out), .C(clk), .Q(D_1));  // open: nQ
  D_FF d_ff_4 (.D(or_4_out), .C(clk), .Q(D_0));  // open: nQ
endmodule
