// Digital circuit gated_s_r_latch.dig as structural Verilog
module gated_s_r_latch (
  input  in_5,
  output Q,
  output Q_2,
  output Q_3,
  output Q_4
);

  wire nand_1_out, nand_2_out, R_2_out, R_out, S_2_out, S_out;

  Button S (.out(S_out));
  Button R (.out(R_out));
  Button R_2 (.out(R_2_out));
  Button S_2 (.out(S_2_out));
  nand nand_1 (nand_1_out, S_out, in_5);
  nand nand_2 (nand_2_out, in_5, R_out);
  nor nor_1 (Q_4, R_2_out, Q_3);
  nor nor_2 (Q_3, Q_4, S_2_out);
  nand nand_3 (Q_2, nand_1_out, Q);
  nand nand_4 (Q, Q_2, nand_2_out);
endmodule
