// Digital circuit s_r_latch.dig as structural Verilog
module s_r_latch (
  output out_1,
  output out_2
);

  wire R_out, S_out;

  Button R (.out(R_out));
  Button S (.out(S_out));
  nor nor_1 (out_2, R_out, out_1);
  nor nor_2 (out_1, out_2, S_out);
endmodule
