// Digital circuit tmp.dig as structural Verilog
module tmp (
  input  D,
  input  E,
  output Q,
  output Q_2
);

  wire nand_1_out, nand_2_out;

  nand nand_1 (nand_1_out, D, E);
  nand nand_2 (nand_2_out, E, ~D);  // NAnd
  nand nand_3 (Q, nand_1_out, Q_2);
  nand nand_4 (Q_2, Q, nand_2_out);
endmodule
